# Fritzing sketch thermometer_ESP (saved by Fritzing 0.9.3b)
breadboards: 1

parts:
  U4 = NodeMCU V3.0
  Part1 = Barometric Pressure Sensor - BMP180 Breakout (GY-68)

nets:
  N1: U4.D1, Part1.SCL
  N2: U4.D2, Part1.SDA
  3V3: U4.3V3, Part1.VCC
  N3: U4.GND#6, U4.GND#13, U4.GND#16, U4.GND#33, Part1.GND

custom parts:
  NodeMCU V3.0: ESP8266 based NodeMCU
